// Logisim project IP_core.circ as structural Verilog: 1 circuit, main circuit main
module main (
  input  INC1_DEC0,
  input  LOAD,
  input  [9:0] in_3,
  input  RESET1
);

  wire CLK_out, counter_1_carry, PWM_out;
  wire [9:0] counter_1_q;

  Clock #(.highDuration(100), .lowDuration(900)) PWM (.out(PWM_out));
  Clock CLK (.out(CLK_out));
  // Probe on counter_1_q
  Counter #(.max('h3ff), .width(10)) counter_1 (
    .load(LOAD), .D(in_3), .count(PWM_out), .Q(counter_1_q), .carry(counter_1_carry), .up(INC1_DEC0),
    .clk(CLK_out), .clr(RESET1));
  // Probe on counter_1_carry

  // Notes on the sheet:
  //   Incrementa = 1 Decrementa = 0
endmodule
